# Fritzing sketch ArduinoCourseProjectColorSensor (saved by Fritzing 0.8.0b)
breadboards: 3

parts:
  Onderdeel1 = Arduino Uno (Rev3)
  R1 = Photocell (LDR) [package=THT]
  Onderdeel2 = Arduino Uno (Rev3)
  R2 = Photocell (LDR) [package=THT]
  R3 = Resistor [tolerance=±5% resistance=1k package=THT]
  LED1 = RGB LED (com. cathode, rgb) [package="5 mm [THT]"]
  Onderdeel3 = Arduino Uno (Rev3)

nets:
  N1: Onderdeel1.A0, R1.pin_1
  N2: Onderdeel1.5V, R1.pin_0
  N3: Onderdeel2.A0, R2.pin_1, R3.Pin_0
  N4: Onderdeel2.GND, R3.Pin_1
  N5: Onderdeel2.5V, R2.pin_0
  N6: LED1.red_anode, Onderdeel3.ICSP_MOSI, Onderdeel3.D11_PWM/MOSI
  N7: LED1.common_cathode, Onderdeel3.GND
  N8: LED1.green_anode, Onderdeel3.D10_PWM/SS
  N9: LED1.blue_anode, Onderdeel3.D9_PWM

notes:
  Naief: welke waarde zul je altijd meten op A0?
  De langste pin moet naar GND. De andere pinnen moeten naar een Arduino pin met een golfje
