# Fritzing sketch ArduinoCourseReadInput (saved by Fritzing 0.8.0b)
breadboards: 2

parts:
  A2 = Arduino Uno (Rev3)
  A1 = Arduino Uno (Rev3)
  S1 = Pushbutton [package=THT]
  S3 = Pushbutton [package=THT]
  R1 = Resistor [tolerance=±5% resistance=1k package=THT]

nets:
  N1: A2.A0, S3.leg0, R1.Pin_0
  N2: A2.GND, R1.Pin_1
  N3: A2.5V, S3.leg1
  N4: A1.A0, S1.leg0
  N5: A1.5V, S1.leg1

notes:
  Goed: pull down weerstand
  Goed bedoeld, maar onjuist!
