# Fritzing sketch CapacitiveSensors (saved by Fritzing 0.8.7b)
breadboards: 1

parts:
  RHL = Resistor [tolerance=±5% resistance=1M package=THT]
  RSL = Resistor [tolerance=±5% resistance=1k package=THT]
  RTL = Resistor [tolerance=±5% resistance=0 package=THT]
  Part1 = Arduino Uno (Rev3)
  RHR = Resistor [tolerance=±5% resistance=1M package=THT]
  RSR = Resistor [tolerance=±5% resistance=1k package=THT]
  RTR = Resistor [tolerance=±5% resistance=0 package=THT]

nets:
  N1: RHL.Pin_0, RSL.Pin_1, RTL.Pin_1
  N2: RHL.Pin_1, Part1.D4, RHR.Pin_0
  N3: RSL.Pin_0, Part1.D2
  N4: Part1.D6_PWM, RSR.Pin_1
  N5: RHR.Pin_1, RSR.Pin_0, RTR.Pin_1
