# Fritzing sketch 18_7_pin_piano (saved by Fritzing 0.9.2b)
breadboards: 3

parts:
  Part1 = Arduino Uno (Rev3)
  S1 = Pushbutton [package="[THT]"]
  R1 = Resistor [tolerance=±5% resistance=10k package=THT]
  Part2 = Arduino Uno (Rev3)
  S4 = Pushbutton [package="[THT]"]
  S6 = Pushbutton [package="[THT]"]
  R5 = Resistor [tolerance=±5% resistance=10k package=THT]
  R6 = Resistor [tolerance=±5% resistance=10k package=THT]
  Part3 = Arduino Uno (Rev3)
  S7 = Pushbutton [package="[THT]"]
  S8 = Pushbutton [package="[THT]"]
  S9 = Pushbutton [package="[THT]"]
  R7 = Resistor [tolerance=±5% resistance=10k package=THT]
  R8 = Resistor [tolerance=±5% resistance=10k package=THT]
  R9 = Resistor [tolerance=±5% resistance=10k package=THT]

nets:
  N1: Part1.GND, R1.Pin_1
  N2: Part1.D2, S1.Pin_1, S1.Pin_2, R1.Pin_0
  N3: Part1.5V, S1.Pin_3, S1.Pin_4
  N4: Part2.GND, R5.Pin_1, R6.Pin_1
  N5: Part2.D2, S4.Pin_1, S4.Pin_2, R5.Pin_0
  N6: Part2.D3_PWM, S6.Pin_1, S6.Pin_2, R6.Pin_0
  N7: Part2.5V, S4.Pin_3, S4.Pin_4, S6.Pin_3, S6.Pin_4
  N8: Part3.GND, R7.Pin_1, R8.Pin_1, R9.Pin_1
  N9: Part3.D2, S9.Pin_1, S9.Pin_2, R8.Pin_0
  N10: Part3.D3_PWM, S8.Pin_1, S8.Pin_2, R7.Pin_0
  N11: Part3.D4, S7.Pin_1, S7.Pin_2, R9.Pin_0
  N12: Part3.5V, S7.Pin_3, S7.Pin_4, S8.Pin_3, S8.Pin_4, S9.Pin_3, S9.Pin_4

notes:
  10 kOhm
  Bruin-Zwart-Oranje-Goud
