# Fritzing sketch 1c_MeerKleurFadeMetFor (saved by Fritzing 0.9.2b)
breadboards: 1

parts:
  LED1 = RGB LED (com. cathode, rgb) [package="5 mm [THT]"]
  R1 = Resistor [tolerance=±5% resistance=1k package=THT]
  R2 = Resistor [tolerance=±5% resistance=1k package=THT]
  R3 = Resistor [tolerance=±5% resistance=1k package=THT]
  Part1 = Arduino Uno (Rev3)

nets:
  N1: LED1.red_anode, R1.Pin_0
  N2: LED1.common_cathode, Part1.GND
  N3: LED1.green_anode, R2.Pin_0
  N4: LED1.blue_anode, R3.Pin_0
  N5: R1.Pin_1, Part1.D11_PWM/MOSI
  N6: R2.Pin_1, Part1.D10_PWM/SS
  N7: R3.Pin_1, Part1.D9_PWM

// code stored in the sketch: 1c_MeerKleurFadeFor.ino
int pin_rood = 9;

void setup()
{
  pinMode(pin_rood, OUTPUT);
}

void loop()
{
  for (int i = 0; i!=256; ++i)
  {
    analogWrite(pin_rood, i);
    delay(30);
  }
}
