# Fritzing sketch 20 (saved by Fritzing 0.9.3b)
circuit board: 8.46667cm x 5.64444cm
breadboards: 4

parts:
  S1 = Pushbutton [package="[THT]"]
  S2 = Pushbutton [package="[THT]"]
  S3 = Pushbutton [package="[THT]"]
  S4 = Pushbutton [package="[THT]"]
  S5 = Pushbutton [package="[THT]"]
  S6 = Pushbutton [package="[THT]"]
  S7 = Pushbutton [package="[THT]"]
  R1 = Resistor [tolerance=±5% resistance=10k package=THT]
  R2 = Resistor [tolerance=±5% resistance=10k package=THT]
  R3 = Resistor [tolerance=±5% resistance=10k package=THT]
  R4 = Resistor [tolerance=±5% resistance=10k package=THT]
  R5 = Resistor [tolerance=±5% resistance=10k package=THT]
  R6 = Resistor [tolerance=±5% resistance=10k package=THT]
  R7 = Resistor [tolerance=±5% resistance=10k package=THT]
  Part1 = Arduino Uno (Rev3)
  R8 = Resistor [tolerance=±5% resistance=10k package=THT]
  Part2 = Arduino Uno (Rev3)
  S8 = Pushbutton [package="[THT]"]
  S9 = Pushbutton [package="[THT]"]
  S10 = Pushbutton [package="[THT]"]
  S11 = Pushbutton [package="[THT]"]
  S12 = Pushbutton [package="[THT]"]
  S13 = Pushbutton [package="[THT]"]
  R9 = Resistor [tolerance=±5% resistance=10k package=THT]
  R11 = Resistor [tolerance=±5% resistance=10k package=THT]
  R12 = Resistor [tolerance=±5% resistance=10k package=THT]
  R13 = Resistor [tolerance=±5% resistance=10k package=THT]
  R14 = Resistor [tolerance=±5% resistance=10k package=THT]
  R15 = Resistor [tolerance=±5% resistance=10k package=THT]
  R16 = Resistor [tolerance=±5% resistance=10k package=THT]
  Part3 = Arduino Uno (Rev3)
  S14 = Pushbutton [package="[THT]"]
  S15 = Pushbutton [package="[THT]"]
  S16 = Pushbutton [package="[THT]"]
  S17 = Pushbutton [package="[THT]"]
  S18 = Pushbutton [package="[THT]"]
  R17 = Resistor [tolerance=±5% resistance=10k package=THT]
  R19 = Resistor [tolerance=±5% resistance=10k package=THT]
  R20 = Resistor [tolerance=±5% resistance=10k package=THT]
  R21 = Resistor [tolerance=±5% resistance=10k package=THT]
  R22 = Resistor [tolerance=±5% resistance=10k package=THT]
  R23 = Resistor [tolerance=±5% resistance=10k package=THT]
  Part4 = Arduino Uno (Rev3)
  S19 = Pushbutton [package="[THT]"]
  S20 = Pushbutton [package="[THT]"]
  S21 = Pushbutton [package="[THT]"]
  S22 = Pushbutton [package="[THT]"]
  R24 = Resistor [tolerance=±5% resistance=10k package=THT]
  R26 = Resistor [tolerance=±5% resistance=10k package=THT]
  R27 = Resistor [tolerance=±5% resistance=10k package=THT]
  R28 = Resistor [tolerance=±5% resistance=10k package=THT]
  R29 = Resistor [tolerance=±5% resistance=10k package=THT]
  J1 = Piezo Speaker

nets:
  N1: S1.Pin_1, S1.Pin_2, S2.Pin_1, S2.Pin_2, S3.Pin_1, S3.Pin_2, S4.Pin_1, S4.Pin_2, S5.Pin_1, S5.Pin_2, S6.Pin_1, S6.Pin_2, S7.Pin_1, S7.Pin_2, Part1.A0, R8.Pin_0
  N2: S1.Pin_3, S1.Pin_4, R1.Pin_0, Part1.GND
  N3: S2.Pin_3, S2.Pin_4, R1.Pin_1, R2.Pin_0
  N4: S3.Pin_3, S3.Pin_4, R2.Pin_1, R3.Pin_0
  N5: S4.Pin_3, S4.Pin_4, R3.Pin_1, R4.Pin_0
  N6: S5.Pin_3, S5.Pin_4, R4.Pin_1, R5.Pin_0
  N7: S6.Pin_3, S6.Pin_4, R5.Pin_1, R6.Pin_0
  N8: S7.Pin_3, S7.Pin_4, R6.Pin_1, R7.Pin_0
  N9: R7.Pin_1, Part1.5V, R8.Pin_1
  N10: Part2.A0, S8.Pin_1, S8.Pin_2, S9.Pin_1, S9.Pin_2, S10.Pin_1, S10.Pin_2, S11.Pin_1, S11.Pin_2, S12.Pin_1, S12.Pin_2, S13.Pin_1, S13.Pin_2, R9.Pin_1
  N11: Part2.5V, R9.Pin_0, R11.Pin_1
  N12: Part2.GND, S8.Pin_3, S8.Pin_4, R16.Pin_0
  N13: S9.Pin_3, S9.Pin_4, R15.Pin_0, R16.Pin_1
  N14: S10.Pin_3, S10.Pin_4, R14.Pin_0, R15.Pin_1
  N15: S11.Pin_3, S11.Pin_4, R13.Pin_0, R14.Pin_1
  N16: S12.Pin_3, S12.Pin_4, R12.Pin_0, R13.Pin_1
  N17: S13.Pin_3, S13.Pin_4, R11.Pin_0, R12.Pin_1
  N18: Part3.A0, S14.Pin_1, S14.Pin_2, S15.Pin_1, S15.Pin_2, S16.Pin_1, S16.Pin_2, S17.Pin_1, S17.Pin_2, S18.Pin_1, S18.Pin_2, R17.Pin_1
  N19: Part3.5V, R17.Pin_0, R19.Pin_1
  N20: Part3.GND, S14.Pin_3, S14.Pin_4, R23.Pin_0
  N21: S15.Pin_3, S15.Pin_4, R22.Pin_0, R23.Pin_1
  N22: S16.Pin_3, S16.Pin_4, R21.Pin_0, R22.Pin_1
  N23: S17.Pin_3, S17.Pin_4, R20.Pin_0, R21.Pin_1
  N24: S18.Pin_3, S18.Pin_4, R19.Pin_0, R20.Pin_1
  N25: Part4.A0, S19.Pin_1, S19.Pin_2, S20.Pin_1, S20.Pin_2, S21.Pin_1, S21.Pin_2, S22.Pin_1, S22.Pin_2
  N26: Part4.GND, S19.Pin_3, S19.Pin_4, R24.Pin_0, R29.Pin_0
  N27: S20.Pin_3, S20.Pin_4, R28.Pin_0, R29.Pin_1
  N28: S21.Pin_3, S21.Pin_4, R27.Pin_0, R28.Pin_1
  N29: S22.Pin_3, S22.Pin_4, R26.Pin_0, R27.Pin_1
  N30: R24.Pin_1, J1.pin1
  N31: R26.Pin_1, J1.pin2

notes:
  Alle weerstanden:
  10 kOhm
  Bruin-Zwart-Oranje-Goud
