# Fritzing sketch 23_theremin_infrarood (saved by Fritzing 0.9.3b)
circuit board: 8.46667cm x 5.64444cm
breadboards: 1

parts:
  J1 = Piezo Speaker
  Part1 = Arduino Uno (Rev3)
  R4 = Resistor [tolerance=±5% resistance=10k package=THT]
  J2 = Infrared Proximity Sensor
  J3 = Infrared Proximity Sensor

nets:
  GND: J1.pin1, Part1.GND, J2.GND, J3.GND
  N1: J1.pin2, R4.Pin_1
  N2: Part1.A0, J2.Vout
  N3: Part1.A1, J3.Vout
  N4: Part1.D5_PWM, R4.Pin_0
  VCC: Part1.5V, J2.Vcc, J3.Vcc

notes:
  Weerstand: 10 kOhm
  bruin-zwart-oranje-goud
