# Fritzing sketch 4_FSR_met_servo (saved by Fritzing 0.9.3b)
breadboards: 2

parts:
  Part1 = Arduino Uno (Rev3)
  R2 = Resistor [tolerance=±5% resistance=10k package=THT]
  J1 = Basic Force Sensing Resistor (FSR) [package=THT]
  Part2 = Arduino Uno (Rev3)
  R3 = Resistor [tolerance=±5% resistance=10k package=THT]
  J2 = Basic Force Sensing Resistor (FSR) [package=THT]
  J3 = Basic Servo

nets:
  N1: Part1.A0, R2.Pin_1, J1.pin_1
  N2: Part1.D9_PWM, J3.pulse
  GND: Part1.GND, R2.Pin_0, J3.gnd
  5V: Part1.5V, J1.pin_0, J3.vcc
  N3: Part2.A0, R3.Pin_1, J2.pin_1
  N4: Part2.GND, R3.Pin_0
  N5: Part2.5V, J2.pin_0
