# Fritzing sketch 5_dc_motor_met_transistor (saved by Fritzing 0.9.2b)
breadboards: 2

parts:
  Part1 = Arduino Uno (Rev3)
  S1 = Pushbutton [package="[THT]"]
  LED1 = LED - 5mm [color="Red (633nm)" package="5 mm [THT]"]
  R1 = Resistor [tolerance=±5% resistance=1k package=THT]
  Part2 = Arduino Uno (Rev3)
  LED2 = LED - 5mm [color="Red (633nm)" package="5 mm [THT]"]
  R2 = Resistor [tolerance=±5% resistance=1k package=THT]
  Q1 = NPN-Transistor [package="TO92 [THT]"]
  R3 = Resistor [tolerance=±5% resistance=1k package=THT]

nets:
  N1: Part1.5V, S1.Pin_3, S1.Pin_4
  N2: Part1.GND, R1.Pin_1
  N3: S1.Pin_1, S1.Pin_2, LED1.anode
  N4: LED1.cathode, R1.Pin_0
  N5: Part2.D13/SCK, R3.Pin_1
  N6: Part2.5V, Q1.E
  N7: Part2.GND, R2.Pin_1
  N8: LED2.cathode, R2.Pin_0
  N9: LED2.anode, Q1.C
  N10: Q1.B, R3.Pin_0
